# Fritzing sketch arduinocade_pro_mini (saved by Fritzing 0.8.7b)
breadboards: 1

parts:
  Part1 = Arduino Pro Mini v13
  R5 = Resistor [tolerance=±5% resistance=1k package=THT]
  R1 = Resistor [tolerance=±5% resistance=470 package=THT]
  R6 = Resistor [tolerance=±5% resistance=100k package=THT]
  U4 = Mystery Part - 3 pins [part_number=TSOP1822 chip_label=IR package=THT]
  C1 = Ceramic Capacitor [capacitance=100nF package="100 mil [THT, multilayer]"]

nets:
  N1: Part1.D0/TX, R1.Pin_0
  VCC: Part1.VCC, U4.VCC
  GND: Part1.GND, U4.GND
  N2: Part1.RESET, C1.0
  N3: Part1.D9_PWM, R5.Pin_0
  N4: Part1.D8, U4.OUT
  N5: Part1.D6_PWM, R6.Pin_0
  N6: R5.Pin_1, R1.Pin_1

notes:
  Video
  Gnd
  Audio
  Arduinocade
  Pro Mini + 28Mhz
  DTR*
  5V
  RXI
  TXO

custom parts:
  Mystery Part - 3 pins: A dummy, proxy, ersatz, stand-in part for whatever you want. With 3 pins on a 100 mil inline pin header footprint.
